# Fritzing sketch bb01v01 (saved by Fritzing 0.9.3b)
circuit board: 8.46667cm x 5.64444cm
breadboards: 1

parts:
  U1 = Adafruit Trinket 5V
  R1 = Resistor [tolerance=±5% resistance=470 package="2010 [SMD]"]
  BATT1 = 3xAAA Switchable Battery Pack w/Bare Wire
  S2 = Pushbutton [package="[THT]"]
  S1 = Pushbutton [package="[THT]"]
  J1 = JST-VHR-3N [part_number=JST-VHR-3N package=THT]
  R3 = Resistor [tolerance=±5% resistance=470 package="2010 [SMD]"]
  R2 = Resistor [tolerance=±5% resistance=470 package="2010 [SMD]"]
  C1 = Electrolytic Capacitor [capacitance=1mF package="200 mil [THT, electrolytic]"]

nets (from the pcb view):
  N1: U1.VBAT, BATT1.POS, J1.pin2, J1.pin_5, C1.-
  N2: U1.GND, R3.Pin_0, R2.Pin_0, C1.+
  N3: U1.#1, S2.Pin_1, S2.Pin_2, R3.Pin_1
  N4: U1.#2, S1.Pin_3, S1.Pin_4, R2.Pin_1
  N5: U1.#0, R1.Pin_1
  N6: U1.+5V, S2.Pin_3, S2.Pin_4, S1.Pin_1, S1.Pin_2
  N7: R1.Pin_0, J1.pin1, J1.pin_4
  N8: BATT1.NEG, J1.pin3, J1.pin_6

custom parts:
  Adafruit Trinket 5V: Trinket may be small, but do not be fooled by its size! It's a tiny microcontroller board, built around the Atmel ATtiny85, a little chip with a lot of power. We wanted to design a microcontroller board that was small enough to fit into any project, and low cost enough to use without hesitation. Perfect for when you don't want to give up your expensive dev-board and you aren't willing to take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
  3xAAA Switchable Battery Pack w/Bare Wire: 3xAAA Switchable Battery Pack w/Bare Wire Connectors
